# Fritzing sketch frame-on-off-on (saved by Fritzing 1.0.4)
circuit board: 3.99999cm x 11cm
breadboards: 3

parts:
  ][1 = PJ-301M [part_number=PJ-301M]
  104 = Ceramic Capacitor [capacitance=100nF voltage=16V package="200 mil [THT, multilayer]"]
  J3 = shrouded pin header, 16 pins [form="♂ (shrouded male)"]
  4001 = Diode [package=diode-1n4148]
  Out1 = PJ-301M [part_number=PJ-301M]
  OUT2 = PJ-301M [part_number=PJ-301M]
  ][2 = PJ-301M [part_number=PJ-301M]
  Out3 = PJ-301M [part_number=PJ-301M]
  ][3 = PJ-301M [part_number=PJ-301M]
  ][4 = PJ-301M [part_number=PJ-301M]
  Rel = Rotary Potentiometer (Small) [maximum_resistance=100kΩ knob_status=50% power=0.5W package=THT]
  Att = Rotary Potentiometer (Small) [maximum_resistance=100kΩ knob_status=50% power=0.5W package=THT]
  OUT4 = PJ-301M [part_number=PJ-301M]
  100uF = Electrolytic Capacitor [capacitance=0.1mF voltage=35V package="100 mil [THT, electrolytic]"]
  220k = Resistor [tolerance=±1% power=0.25W resistance=220k package=THT]
  BAT46 = Diode [package=diode-1n4148]
  BAT46_2 = Diode [package=diode-1n4148]
  BAT46_3 = Diode [package=diode-1n4148]
  BAT46_4 = Diode [package=diode-1n4148]
  6_8n = Ceramic Capacitor [capacitance=2.2nF voltage=16V package="200 mil [THT, multilayer]"]
  2_2n = Ceramic Capacitor [capacitance=2.2nF voltage=16V package="200 mil [THT, multilayer]"]
  2_2n_2 = Ceramic Capacitor [capacitance=2.2nF voltage=16V package="200 mil [THT, multilayer]"]
  120k = Resistor [tolerance=±1% power=0.25W resistance=100k package=THT]
  120k_2 = Resistor [tolerance=±1% power=0.25W resistance=100k package=THT]
  120k_3 = Resistor [tolerance=±1% power=0.25W resistance=100k package=THT]
  1M = Resistor [tolerance=±1% power=0.25W resistance=1M package=THT]
  1M_2 = Resistor [tolerance=±1% power=0.25W resistance=1M package=THT]
  1M_3 = Resistor [tolerance=±1% power=0.25W resistance=1M package=THT]
  1M_4 = Resistor [tolerance=±1% power=0.25W resistance=1M package=THT]
  4_7n = Ceramic Capacitor [capacitance=4.7nF voltage=16V package="200 mil [THT, multilayer]"]
  4_7n_2 = Ceramic Capacitor [capacitance=4.7nF voltage=16V package="200 mil [THT, multilayer]"]
  10nF = Ceramic Capacitor [capacitance=10nF voltage=16V package="200 mil [THT, multilayer]"]
  120k_4 = Resistor [tolerance=±1% power=0.25W resistance=100k package=THT]
  120k_5 = Resistor [tolerance=±1% power=0.25W resistance=100k package=THT]
  10K = Resistor [tolerance=±1% power=0.25W resistance=10k package=THT]
  4_7n_3 = Ceramic Capacitor [capacitance=4.7nF voltage=16V package="200 mil [THT, multilayer]"]
  4_7n_4 = Ceramic Capacitor [capacitance=4.7nF voltage=16V package="200 mil [THT, multilayer]"]
  120k_6 = Resistor [tolerance=±1% power=0.25W resistance=100k package=THT]
  120k_7 = Resistor [tolerance=±1% power=0.25W resistance=100k package=THT]
  22nF = Ceramic Capacitor [capacitance=22nF voltage=16V package="200 mil [THT, multilayer]"]
  10nF_2 = Ceramic Capacitor [capacitance=10nF voltage=16V package="200 mil [THT, multilayer]"]
  10nF_3 = Ceramic Capacitor [capacitance=10nF voltage=16V package="200 mil [THT, multilayer]"]
  10nF_4 = Ceramic Capacitor [capacitance=2.2nF voltage=16V package="200 mil [THT, multilayer]"]
  120k_8 = Resistor [tolerance=±1% power=0.25W resistance=100k package=THT]
  10K_2 = Resistor [tolerance=±1% power=0.25W resistance=10k package=THT]
  120k_9 = Resistor [tolerance=±1% power=0.25W resistance=100k package=THT]
  Mix = PJ-301M [part_number=PJ-301M]
  100nF = Film/Foil Capacitor [capacitance=100nF voltage=35V package="5mm [THT, pp]"]
  100nF1 = Film/Foil Capacitor [capacitance=100nF voltage=35V package="5mm [THT, pp]"]
  10K_3 = Resistor [tolerance=±1% power=0.25W resistance=10k package=THT]
  100n = Ceramic Capacitor [capacitance=100nF voltage=16V package="200 mil [THT, multilayer]"]
  33n = Ceramic Capacitor [capacitance=22nF voltage=16V package="200 mil [THT, multilayer]"]
  33nF = Ceramic Capacitor [capacitance=22nF voltage=16V package="200 mil [THT, multilayer]"]
  33nF_2 = Ceramic Capacitor [capacitance=22nF voltage=16V package="200 mil [THT, multilayer]"]
  120k_10 = Resistor [tolerance=±1% power=0.25W resistance=100k package=THT]
  10K_4 = Resistor [tolerance=±1% power=0.25W resistance=10k package=THT]
  120k_11 = Resistor [tolerance=±1% power=0.25W resistance=100k package=THT]
  470nF = Film/Foil Capacitor [capacitance=100nF voltage=35V package="5mm [THT, pp]"]
  100nF3 = Film/Foil Capacitor [capacitance=100nF voltage=35V package="5mm [THT, pp]"]
  10K_5 = Resistor [tolerance=±5% power=0.25W resistance=10k package=THT]
  10K_6 = Resistor [tolerance=±5% power=0.25W resistance=10k package=THT]
  4_7K = Resistor [tolerance=±5% power=0.25W resistance=4.7k package=THT]
  4_7n_5 = Ceramic Capacitor [capacitance=4.7nF voltage=16V package="200 mil [THT, multilayer]"]
  4_7n_6 = Ceramic Capacitor [capacitance=4.7nF voltage=16V package="200 mil [THT, multilayer]"]
  4_7n_7 = Ceramic Capacitor [capacitance=4.7nF voltage=16V package="200 mil [THT, multilayer]"]
  4_7n_8 = Ceramic Capacitor [capacitance=4.7nF voltage=16V package="200 mil [THT, multilayer]"]
  1K = Resistor [tolerance=±1% power=0.25W resistance=47k package=THT]
  1K_2 = Resistor [tolerance=±1% power=0.25W resistance=47k package=THT]
  J4 = female pin header, 1 pin [form="♀ (female)"]
  S2 = Taiway 100-SP-X-T1 SPDT Miniature Toggle Switch [part_number=100-SP-X-T1-0-0-B1-M2 package=THT]
  6_8n_2 = Ceramic Capacitor [capacitance=4.7nF voltage=16V package="200 mil [THT, multilayer]"]
  S3 = Taiway 100-SP-X-T1 SPDT Miniature Toggle Switch [part_number=100-SP-X-T1-0-0-B1-M2 package=THT]
  22nF1 = Ceramic Capacitor [capacitance=22nF voltage=16V package="200 mil [THT, multilayer]"]
  103 = Ceramic Capacitor [capacitance=10nF voltage=16V package="200 mil [THT, multilayer]"]
  U2 = Quad Norton Op Amp [part_number=LM3900 package="DIP (Dual Inline) [THT]"]
  part = Quad Norton Op Amp [part_number=LM3900 package="DIP (Dual Inline) [THT]"]  # not connected
  U2_1 = Quad Norton Op Amp [part_number=LM3900 package="DIP (Dual Inline) [THT]"]  # not connected
  U2_2 = Quad Norton Op Amp [part_number=LM3900 package="DIP (Dual Inline) [THT]"]  # not connected
  U2_3 = Quad Norton Op Amp [part_number=LM3900 package="DIP (Dual Inline) [THT]"]  # not connected
  U2_4 = Quad Norton Op Amp [part_number=LM3900 package="DIP (Dual Inline) [THT]"]  # not connected
  S4 = Taiway 100-SP-X-T1 SPDT Miniature Toggle Switch [part_number=100-SP-X-T1-0-0-B1-M2 package=THT]
  2_2n_3 = Ceramic Capacitor [capacitance=2.2nF voltage=16V package="200 mil [THT, multilayer]"]
  J5 = female pin header, 1 pin [form="♀ (female)"]
  S5 = Taiway 100-SP-X-T1 SPDT Miniature Toggle Switch [part_number=100-SP-X-T1-0-0-B1-M2 package=THT]
  33n_2 = Ceramic Capacitor [capacitance=22nF voltage=16V package="200 mil [THT, multilayer]"]

nets:
  GND: ][1.Pin_1, 104.1, J3.pin2, J3.pin3, J3.pin4, J3.pin13, J3.pin14, J3.pin15, Out1.Pin_1, OUT2.Pin_1, ][2.Pin_1, Out3.Pin_1, ][3.Pin_1, ][4.Pin_1, OUT4.Pin_1, 100uF.-, 10K.Pin_0, 10K_2.Pin_1, Mix.Pin_1, 10K_3.Pin_1, 10K_4.Pin_0, J4.pin1, 103.1, U2.connector6
  N1: ][1.Pin_3, 4_7n_5.1
  N2: 104.0, 4001.C, 100uF.+, 1M.Pin_0, 1M_2.Pin_0, 1M_3.Pin_0, 1M_4.Pin_0, 103.0, U2.connector13, J5.pin1
  N3: J3.pin1, J3.pin16
  9V: J3.pin5, J3.pin6, J3.pin11, J3.pin12, 4001.A
  N4: J3.pin7, J3.pin10
  N5: J3.pin8, J3.pin9
  N6: Out1.Pin_2, Rel.leg1
  N7: Out1.Pin_3, 10K_5.Pin_1
  N8: OUT2.Pin_2, Rel.leg2
  N9: OUT2.Pin_3, 10K_6.Pin_1
  N10: ][2.Pin_3, 4_7n_7.0
  N11: Out3.Pin_2, Att.leg1
  N12: Out3.Pin_3, 4_7K.Pin_1
  N13: ][3.Pin_3, 4_7n_6.1
  N14: ][4.Pin_3, 4_7n_8.0
  N15: Rel.wiper, 1K.Pin_0
  N16: Att.wiper, 1K_2.Pin_1
  N17: Att.leg2, OUT4.Pin_2
  N18: OUT4.Pin_3, 470nF.-
  N19: 220k.Pin_0, 33nF_2.0, 120k_10.Pin_0, U2.connector10
  N20: 220k.Pin_1, BAT46.C
  N21: BAT46.A, 4_7n_8.1
  N22: BAT46_2.A, 4_7n_7.1
  N23: BAT46_2.C, 120k_3.Pin_0
  N24: BAT46_3.A, 4_7n_6.0
  N25: BAT46_3.C, 120k.Pin_1
  N26: BAT46_4.A, 4_7n_5.0
  N27: BAT46_4.C, 120k_2.Pin_1
  N28: 6_8n.0, 2_2n.0, 2_2n_2.0, 4_7n.1, 10K.Pin_1, 2_2n_3.0
  N29: 6_8n.1, S4.L2
  N30: 2_2n.1, 120k_2.Pin_0, 120k_5.Pin_1, U2.connector5
  N31: 2_2n_2.1, 120k_4.Pin_1, 100nF.+, U2.connector4
  N32: 120k.Pin_0, 10nF_4.0, 120k_8.Pin_0, U2.connector7
  N33: 120k_3.Pin_1, 4_7n_3.0, 120k_7.Pin_0, U2.connector2
  N34: 1M.Pin_1, U2.connector0
  N35: 1M_2.Pin_1, U2.connector1
  N36: 1M_3.Pin_1, U2.connector12
  N37: 1M_4.Pin_1, U2.connector11
  N38: 4_7n.0, S4.L1
  N39: 4_7n_2.0, 10nF.1, 4_7n_3.1, 4_7n_4.1, 10K_3.Pin_0, 6_8n_2.0
  N40: 4_7n_2.1, S2.L2
  N41: 10nF.0, S2.L1
  N42: 120k_4.Pin_0, 120k_5.Pin_0, S4.COM, 2_2n_3.1
  N43: 4_7n_4.0, 120k_6.Pin_0, 100nF1.+, U2.connector3
  N44: 120k_6.Pin_1, 120k_7.Pin_1, S2.COM, 6_8n_2.1
  N45: 22nF.0, S3.L1
  N46: 22nF.1, 10nF_2.0, 10nF_3.1, 10nF_4.1, 10K_2.Pin_0, 22nF1.0
  N47: 10nF_2.1, S3.L2
  N48: 10nF_3.0, 120k_9.Pin_0, 100nF3.+, U2.connector8
  N49: 120k_8.Pin_1, 120k_9.Pin_1, S3.COM, 22nF1.1
  N50: Mix.Pin_3, 1K.Pin_1, 1K_2.Pin_0
  N51: 100nF.-, 10K_5.Pin_0
  N52: 100nF1.-, 10K_6.Pin_0
  N53: 100n.0, S5.L1
  N54: 100n.1, 33n.0, 33nF.1, 33nF_2.1, 120k_10.Pin_1, 10K_4.Pin_1, 120k_11.Pin_1, S5.COM, 33n_2.0, 33n_2.1
  N55: 33n.1, S5.L2
  N56: 33nF.0, 120k_11.Pin_0, 470nF.+, U2.connector9
  N57: 100nF3.-, 4_7K.Pin_0

notes:
  frame
  blueprint@poetaster . de 2025
  jlcjlcjlcjlcjlc

custom parts:
  PJ-301M: Phone power jack.
  Quad Norton Op Amp: LM3900 Quad Norton Op Amp.
  Quad Norton Op Amp: LM3900 Quad Norton Op Amp.
  Quad Norton Op Amp: LM3900 Quad Norton Op Amp.
  Quad Norton Op Amp: LM3900 Quad Norton Op Amp.
  Quad Norton Op Amp: LM3900 Quad Norton Op Amp.
  Quad Norton Op Amp: LM3900 Quad Norton Op Amp.
