# Fritzing sketch frame (saved by Fritzing 1.0.4)
circuit board: 3.99999cm x 11cm
breadboards: 3

parts:
  ][1 = PJ-301M [part_number=PJ-301M]
  103 = Ceramic Capacitor [capacitance=10nF voltage=16V package="200 mil [THT, multilayer]"]
  104 = Ceramic Capacitor [capacitance=100nF voltage=16V package="200 mil [THT, multilayer]"]
  J3 = shrouded pin header, 16 pins [form="♂ (shrouded male)"]
  4001 = Diode [package=diode-1n4148]
  Out1 = PJ-301M [part_number=PJ-301M]
  OUT2 = PJ-301M [part_number=PJ-301M]
  ][2 = PJ-301M [part_number=PJ-301M]
  Out3 = PJ-301M [part_number=PJ-301M]
  IN3 = PJ-301M [part_number=PJ-301M]
  IN4 = PJ-301M [part_number=PJ-301M]
  Rel = Rotary Potentiometer (Small) [maximum_resistance=100kΩ knob_status=50% power=0.5W package=THT]
  Att = Rotary Potentiometer (Small) [maximum_resistance=100kΩ knob_status=50% power=0.5W package=THT]
  OUT4 = PJ-301M [part_number=PJ-301M]
  100uF = Electrolytic Capacitor [capacitance=0.1mF voltage=35V package="100 mil [THT, electrolytic]"]
  120k = Resistor [tolerance=±1% power=0.25W resistance=100k package=THT]
  1N1418 = Diode [package=diode-1n4148]
  1N1418_2 = Diode [package=diode-1n4148]
  1N1418_3 = Diode [package=diode-1n4148]
  1N1418_4 = Diode [package=diode-1n4148]
  2_2n = Ceramic Capacitor [capacitance=2.2nF voltage=16V package="200 mil [THT, multilayer]"]
  2_2n_2 = Ceramic Capacitor [capacitance=2.2nF voltage=16V package="200 mil [THT, multilayer]"]
  2_2n_3 = Ceramic Capacitor [capacitance=2.2nF voltage=16V package="200 mil [THT, multilayer]"]
  120k_2 = Resistor [tolerance=±1% power=0.25W resistance=100k package=THT]
  120k_3 = Resistor [tolerance=±1% power=0.25W resistance=100k package=THT]
  120k_4 = Resistor [tolerance=±1% power=0.25W resistance=100k package=THT]
  1M = Resistor [tolerance=±1% power=0.25W resistance=1M package=THT]
  1M_2 = Resistor [tolerance=±1% power=0.25W resistance=1M package=THT]
  1M_3 = Resistor [tolerance=±1% power=0.25W resistance=1M package=THT]
  1M_4 = Resistor [tolerance=±1% power=0.25W resistance=1M package=THT]
  4_7n = Ceramic Capacitor [capacitance=4.7nF voltage=16V package="200 mil [THT, multilayer]"]
  4_7n_2 = Ceramic Capacitor [capacitance=4.7nF voltage=16V package="200 mil [THT, multilayer]"]
  10nF = Ceramic Capacitor [capacitance=10nF voltage=16V package="200 mil [THT, multilayer]"]
  120k_5 = Resistor [tolerance=±1% power=0.25W resistance=100k package=THT]
  120k_6 = Resistor [tolerance=±1% power=0.25W resistance=100k package=THT]
  10K = Resistor [tolerance=±1% power=0.25W resistance=10k package=THT]
  4_7n_3 = Ceramic Capacitor [capacitance=4.7nF voltage=16V package="200 mil [THT, multilayer]"]
  4_7n_4 = Ceramic Capacitor [capacitance=4.7nF voltage=16V package="200 mil [THT, multilayer]"]
  120k_7 = Resistor [tolerance=±1% power=0.25W resistance=100k package=THT]
  120k4 = Resistor [tolerance=±1% power=0.25W resistance=100k package=THT]
  5||14 = SPST Switch [package=switch-spdt_kit]
  5||13 = SPST Switch [package=switch-spdt_kit]
  22nF = Ceramic Capacitor [capacitance=22nF voltage=16V package="200 mil [THT, multilayer]"]
  10nF_2 = Ceramic Capacitor [capacitance=10nF voltage=16V package="200 mil [THT, multilayer]"]
  5||15 = SPST Switch [package=switch-spdt_kit]
  10nF_3 = Ceramic Capacitor [capacitance=10nF voltage=16V package="200 mil [THT, multilayer]"]
  10nF_4 = Ceramic Capacitor [capacitance=2.2nF voltage=16V package="200 mil [THT, multilayer]"]
  120k_8 = Resistor [tolerance=±1% power=0.25W resistance=100k package=THT]
  10K_2 = Resistor [tolerance=±1% power=0.25W resistance=10k package=THT]
  120k_9 = Resistor [tolerance=±1% power=0.25W resistance=100k package=THT]
  Mix = PJ-301M [part_number=PJ-301M]
  100nF = Film/Foil Capacitor [capacitance=100nF voltage=35V package="5mm [THT, pp]"]
  100nF1 = Film/Foil Capacitor [capacitance=100nF voltage=35V package="5mm [THT, pp]"]
  200K = Resistor [tolerance=±1% power=0.25W resistance=220k package=THT]
  100K = Resistor [tolerance=±5% power=0.25W resistance=100k package=THT]
  100K_2 = Resistor [tolerance=±5% power=0.25W resistance=100k package=THT]
  10K_3 = Resistor [tolerance=±1% power=0.25W resistance=10k package=THT]
  200K_2 = Resistor [tolerance=±1% power=0.25W resistance=220k package=THT]
  5||16 = SPST Switch [package=switch-spdt_kit]
  100nF_2 = Ceramic Capacitor [capacitance=100nF voltage=16V package="200 mil [THT, multilayer]"]
  33nF = Ceramic Capacitor [capacitance=22nF voltage=16V package="200 mil [THT, multilayer]"]
  33nF_2 = Ceramic Capacitor [capacitance=22nF voltage=16V package="200 mil [THT, multilayer]"]
  33nF_3 = Ceramic Capacitor [capacitance=22nF voltage=16V package="200 mil [THT, multilayer]"]
  120k5 = Resistor [tolerance=±1% power=0.25W resistance=100k package=THT]
  10K_4 = Resistor [tolerance=±1% power=0.25W resistance=10k package=THT]
  120k6 = Resistor [tolerance=±1% power=0.25W resistance=100k package=THT]
  072 = TL072 [package="DIP (Dual Inline) [THT]"]
  072_PWR = TL072 [package="DIP (Dual Inline) [THT]"]  # not connected
  072_A = TL072 [package="DIP (Dual Inline) [THT]"]  # not connected
  072_B = TL072 [package="DIP (Dual Inline) [THT]"]  # not connected
  103_2 = Ceramic Capacitor [capacitance=10nF voltage=16V package="200 mil [THT, multilayer]"]
  200K_3 = Resistor [tolerance=±1% power=0.25W resistance=220k package=THT]
  200K2 = Resistor [tolerance=±1% power=0.25W resistance=220k package=THT]
  072_2 = TL072 [package="DIP (Dual Inline) [THT]"]
  072_PWR_2 = TL072 [package="DIP (Dual Inline) [THT]"]  # not connected
  072_A_2 = TL072 [package="DIP (Dual Inline) [THT]"]  # not connected
  072_B_2 = TL072 [package="DIP (Dual Inline) [THT]"]  # not connected
  100K_3 = Resistor [tolerance=±5% power=0.25W resistance=100k package=THT]
  100K_4 = Resistor [tolerance=±5% power=0.25W resistance=100k package=THT]
  100nF2 = Film/Foil Capacitor [capacitance=100nF voltage=35V package="5mm [THT, pp]"]
  100nF3 = Film/Foil Capacitor [capacitance=100nF voltage=35V package="5mm [THT, pp]"]
  Part1 = Quad Norton Op Amp [part_number=LM3900 package="DIP (Dual Inline) [THT]"]  # not connected
  U1_1 = Quad Norton Op Amp [part_number=LM3900 package="DIP (Dual Inline) [THT]"]  # not connected
  U1_2 = Quad Norton Op Amp [part_number=LM3900 package="DIP (Dual Inline) [THT]"]  # not connected
  U1_3 = Quad Norton Op Amp [part_number=LM3900 package="DIP (Dual Inline) [THT]"]  # not connected
  U1_4 = Quad Norton Op Amp [part_number=LM3900 package="DIP (Dual Inline) [THT]"]  # not connected
  U1 = Quad Norton Op Amp [part_number=LM3900 package="DIP (Dual Inline) [THT]"]
  103_3 = Ceramic Capacitor [capacitance=10nF voltage=16V package="200 mil [THT, multilayer]"]

nets:
  GND: ][1.Pin_1, 103.1, 104.1, J3.pin2, J3.pin3, J3.pin4, J3.pin13, J3.pin14, J3.pin15, Out1.Pin_1, OUT2.Pin_1, ][2.Pin_1, Out3.Pin_1, IN3.Pin_1, IN4.Pin_1, OUT4.Pin_1, 100uF.-, 1N1418.C, 1N1418_2.C, 1N1418_3.C, 1N1418_4.C, 10K.Pin_0, 10K_2.Pin_1, Mix.Pin_1, 10K_3.Pin_1, 10K_4.Pin_0, 072.connector3, 103_2.1, 072_2.connector3, U1.connector6, 103_3.1
  N1: ][1.Pin_3, 1N1418_4.A, 120k_3.Pin_0
  N2: 103.0, 104.0, 4001.C, 100uF.+, 1M.Pin_0, 1M_2.Pin_0, 1M_3.Pin_0, 1M_4.Pin_0, 072.connector2, 072.connector4, 072.connector7, 103_2.0, 072_2.connector2, 072_2.connector4, 072_2.connector7, U1.connector13, 103_3.0
  N3: J3.pin1, J3.pin16
  9V: J3.pin5, J3.pin6, J3.pin11, J3.pin12, 4001.A
  N4: J3.pin7, J3.pin10
  N5: J3.pin8, J3.pin9
  N6: Out1.Pin_3, Rel.leg2, 200K.Pin_0, 072.connector0
  N7: OUT2.Pin_3, Rel.leg1, 200K_2.Pin_1, 072.connector6
  N8: ][2.Pin_3, 1N1418_2.A, 120k_4.Pin_0
  N9: Out3.Pin_3, Att.leg2, 200K2.Pin_0, 072_2.connector0
  N10: IN3.Pin_3, 1N1418_3.A, 120k_2.Pin_0
  N11: IN4.Pin_3, 120k.Pin_0, 1N1418.A
  N12: Rel.wiper, Att.wiper, Mix.Pin_3
  N13: Att.leg1, OUT4.Pin_3, 200K_3.Pin_1, 072_2.connector6
  N14: 120k.Pin_1, 10nF_4.0, 120k_8.Pin_0, U1.connector7
  N15: 2_2n.0, 2_2n_2.0, 2_2n_3.0, 4_7n.1, 10K.Pin_1
  N16: 2_2n.1, 5||14.S
  N17: 2_2n_2.1, 120k_3.Pin_1, 120k_6.Pin_1, U1.connector5
  N18: 2_2n_3.1, 120k_5.Pin_1, 100nF.+, U1.connector4
  N19: 120k_2.Pin_1, 33nF_3.0, 120k5.Pin_0, U1.connector10
  N20: 120k_4.Pin_1, 4_7n_3.0, 120k4.Pin_0, U1.connector2
  N21: 1M.Pin_1, U1.connector0
  N22: 1M_2.Pin_1, U1.connector1
  N23: 1M_3.Pin_1, U1.connector12
  N24: 1M_4.Pin_1, U1.connector11
  N25: 4_7n.0, 5||14.O
  N26: 4_7n_2.0, 10nF.1, 4_7n_3.1, 4_7n_4.1, 10K_3.Pin_0
  N27: 4_7n_2.1, 5||13.S
  N28: 10nF.0, 5||13.O
  N29: 120k_5.Pin_0, 120k_6.Pin_0, 5||14.P
  N30: 4_7n_4.0, 120k_7.Pin_0, 100nF1.+, U1.connector3
  N31: 120k_7.Pin_1, 120k4.Pin_1, 5||13.P
  N32: 22nF.0, 5||15.O
  N33: 22nF.1, 10nF_2.0, 10nF_3.1, 10nF_4.1, 10K_2.Pin_0
  N34: 10nF_2.1, 5||15.S
  N35: 5||15.P, 120k_8.Pin_1, 120k_9.Pin_1
  N36: 10nF_3.0, 120k_9.Pin_0, 100nF3.+, U1.connector8
  N37: 100nF.-, 100K_2.Pin_0
  N38: 100nF1.-, 100K.Pin_0
  N39: 200K.Pin_1, 100K_2.Pin_1, 072.connector1
  N40: 100K.Pin_1, 200K_2.Pin_0, 072.connector5
  N41: 5||16.O, 100nF_2.0
  N42: 5||16.P, 120k5.Pin_1, 120k6.Pin_1
  N43: 5||16.S, 33nF.1
  N44: 100nF_2.1, 33nF.0, 33nF_2.1, 33nF_3.1, 10K_4.Pin_1
  N45: 33nF_2.0, 120k6.Pin_0, 100nF2.+, U1.connector9
  N46: 200K_3.Pin_0, 072_2.connector5, 100K_4.Pin_1
  N47: 200K2.Pin_1, 072_2.connector1, 100K_3.Pin_1
  N48: 100K_3.Pin_0, 100nF3.-
  N49: 100K_4.Pin_0, 100nF2.-

notes:
  frame
  blueprint@poetaster . de 2025
  jlcjlcjlcjlcjlc

custom parts:
  PJ-301M: Phone power jack.
  TL072: Dual Operational Amplifier
  TL072: Dual Operational Amplifier
  TL072: Dual Operational Amplifier
  TL072: Dual Operational Amplifier
  Quad Norton Op Amp: LM3900 Quad Norton Op Amp.
  Quad Norton Op Amp: LM3900 Quad Norton Op Amp.
  Quad Norton Op Amp: LM3900 Quad Norton Op Amp.
  Quad Norton Op Amp: LM3900 Quad Norton Op Amp.
  Quad Norton Op Amp: LM3900 Quad Norton Op Amp.
  Quad Norton Op Amp: LM3900 Quad Norton Op Amp.
